# Fritzing sketch Schaltplan (saved by Fritzing 0.9.3b)

parts:
  Arduino = Arduino Uno (Rev3) - ICSP
  Bluetooth_Modul = Bluetooth HC-05 Macho
  H-Brücke = Arduino Modkit Shield
  DC_Motor_1 = DC Motor
  DC_Motor_2 = DC Motor
  Bluetooth_Modul1 = Bluetooth HC-05 Macho  # not connected

nets:
  GND: Arduino.GND, Bluetooth_Modul.GND
  N1: Arduino.D8, H-Brücke.A2
  N2: Arduino.D9_PWM, H-Brücke.A1
  N3: Arduino.D10_PWM/SS, H-Brücke.A0
  N4: Arduino.D0/RX, Bluetooth_Modul.TXD
  N5: Arduino.D1/TX, Bluetooth_Modul.RXD
  N6: Arduino.D5_PWM, H-Brücke.A5
  N7: Arduino.D6_PWM, H-Brücke.A4
  N8: Arduino.D7, H-Brücke.A3
  5V: Arduino.5V, Bluetooth_Modul.VCC
  N9: H-Brücke.OUT2, DC_Motor_2.pin_2
  N10: H-Brücke.OUT1, DC_Motor_2.pin_1
  N11: H-Brücke.OUT3, DC_Motor_1.pin_2
  N12: H-Brücke.OUT4, DC_Motor_1.pin_1
